# Fritzing sketch components_diagram (saved by Fritzing 1.0.3b)

parts:
  Mod1 = ESP32-TTGO-T-DISPLAY
  S1 = Round Pushbutton
  S2 = Round Pushbutton

nets:
  N1: Mod1.G-1, Mod1.G-11, Mod1.G-14, S1.leg0, S2.leg1
  N2: Mod1.17, S1.leg1
  N3: Mod1.33, S2.leg0

custom parts:
  ESP32-TTGO-T-DISPLAY: LILYGO TTGO T-Display GD32VF103CBT6 Main Chip ST7789 1.14 Inch IPS 240x135 Resolution Minimalist Development Board.
